# Fritzing sketch electrical (saved by Fritzing 1.0.6)

parts:
  Part1 = TPS62827 Buck Converter [part_number="Adafruit #4920"]
  WeMos_D1_Mini1 = WeMos D1 Mini
  JACK1 = 2.1mm Barrel Jack with Terminal Block
  U1 = L9110 H-bridge module [part_number="L9110 H-bridge"]
  S1 = Toggle Switch [package=THT]
  S2 = Toggle Switch [package=THT]
  M1 = DC Motor [voltage_(max)=6V voltage_(min)=3V]

nets:
  N1: Part1.EN, JACK1.NEG, U1.GND
  VIN: Part1.VIN, JACK1.POS, U1.VCC
  3.3V: Part1.3.3V, WeMos_D1_Mini1.3V3
  N2: Part1.GND, WeMos_D1_Mini1.G, S1.COM, S2.COM
  N3: WeMos_D1_Mini1.D1, U1.B-IA
  N4: WeMos_D1_Mini1.D2, U1.B-IB
  N5: WeMos_D1_Mini1.D5, S1.L2
  N6: WeMos_D1_Mini1.D6, S2.L2
  N7: U1.MOTOR_B-A, M1.pin_2
  N8: U1.MOTOR_B-B, M1.pin_1

custom parts:
  TPS62827 Buck Converter: This little buck converter based on the TPS62827 is super handy, taking up to 5.5V input and providing a 3.3V output with up to 2A current. It's great for supplying power to hungry 3.3V voltage circuits from a range of battery or power options. This chip provides up to 2 Amp load current across the entire input voltage range of 3.4 to 5.5V. It's not a huge range but does cover LiPoly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
